# Fritzing sketch ftdi-arduino-pro-mini-v2 (saved by Fritzing 0.9.2b)

parts:
  Composant1 = FTDI Basic Programmer
  Composant2 = Arduino Pro Mini v13

nets:
  N1: Composant1.DTR, Composant2.DTR
  N2: Composant1.RXI, Composant2.D0/TX
  N3: Composant1.TXO, Composant2.D1/RX
  N4: Composant1.POWER, Composant2.VCC
  GND: Composant1.GND, Composant2.GND
