# Fritzing sketch gateway-serial (saved by Fritzing 0.9.2b)

parts:
  Composant1 = Arduino Nano (Rev3.0) (ICSP)
  NRF24L1 = NRF24L01

nets:
  N1: Composant1.D9, NRF24L1.CE
  N2: Composant1.D10, NRF24L1.CSN
  N3: Composant1.D11/MOSI, NRF24L1.MOSI
  N4: Composant1.D12/MISO, NRF24L1.MISO
  GND: Composant1.GND, NRF24L1.GND
  3V3: Composant1.3V3, NRF24L1.VCC
  N5: Composant1.D13/SCK, NRF24L1.SCK

notes:
  NRF24L01+
  IRQ MISO
  MOSI SCK
  CSN CE
  VCC GND

custom parts:
  NRF24L01: NRF24L01 module
